// Logisim project 4BitRegister.circ as structural Verilog: 1 circuit, main circuit main
module main (
  input  Clock,
  input  Data_Input_D3,
  input  Control__Enable,
  input  Data_Input_D2,
  input  Data_Input_D1,
  input  Data_Input_D0,
  output Q1,
  output Q2,
  output Q3,
  output Q0
);

  D_Flip_Flop d_ff_1 (.clk(Clock), .D(Data_Input_D3), .Q(Q1), .en(Control__Enable));  // open: Qn, preset, reset
  D_Flip_Flop d_ff_2 (.clk(Clock), .D(Data_Input_D2), .Q(Q2), .en(Control__Enable));  // open: Qn, preset, reset
  D_Flip_Flop d_ff_3 (.clk(Clock), .D(Data_Input_D1), .Q(Q3), .en(Control__Enable));  // open: Qn, preset, reset
  D_Flip_Flop d_ff_4 (.clk(Clock), .D(Data_Input_D0), .Q(Q0), .en(Control__Enable));  // open: Qn, preset, reset

  // Notes on the sheet:
  //   4 Bit Register
  //   D Flip Flop
  //   D Flip Flop
  //   D Flip Flop
  //   D Flip Flop
endmodule
