// Logisim project ALU.circ as structural Verilog: 1 circuit, main circuit main
module main (
  input  in_1,
  input  [3:0] A,
  input  [3:0] B,
  input  in_4,
  input  [1:0] in_5,
  output out_6,
  output [3:0] out_7,
  output out_8
);

  wire and_5_out, and_6_out, and_7_out, and_8_out, and_9_out, and_10_out, and_11_out, and_12_out, and_13_out,
       and_14_out, and_15_out, and_16_out, and_17_out, and_18_out, and_19_out, and_20_out, or_5_out,
       or_6_out, or_7_out, or_8_out, or_9_out, or_10_out, or_11_out, undriven, undriven_2, xor_1_out,
       xor_2_out, xor_3_out, xor_4_out, xor_5_out, xor_6_out, xor_7_out, xor_8_out, xor_14_out, xor_15_out,
       xor_16_out, xor_17_out;
  wire [3:0] and_4_out, or_4_out, xor_9_out, xor_18_out;

  or or_1 (or_4_out[3], A[3], B[3]);
  or or_2 (or_4_out[2], A[2], B[2]);
  or or_3 (or_4_out[1], A[1], B[1]);
  or or_4 (or_4_out[0], A[0], A[1]);
  and and_1 (and_4_out[3], A[3], B[3]);
  and and_2 (and_4_out[2], A[2], B[2]);
  and and_3 (and_4_out[1], A[1], B[1]);
  and and_4 (and_4_out[0], A[0], A[1]);
  xor xor_1 (xor_1_out, A[1], in_4);
  xor xor_2 (xor_2_out, B[1], in_4);
  xor xor_3 (xor_3_out, B[2], in_4);
  xor xor_4 (xor_4_out, B[3], in_4);
  xor xor_5 (xor_5_out, A[0], xor_1_out);
  and and_5 (and_5_out, xor_1_out, A[0]);
  xor xor_6 (xor_6_out, A[1], xor_2_out);
  and and_6 (and_6_out, xor_2_out, A[1]);
  xor xor_7 (xor_7_out, A[2], xor_3_out);
  and and_7 (and_7_out, xor_3_out, A[2]);
  xor xor_8 (xor_8_out, A[3], xor_4_out);
  and and_8 (and_8_out, xor_4_out, A[3]);
  xor xor_9 (xor_9_out[0], xor_5_out, in_4);
  and and_9 (and_9_out, xor_5_out, in_4);
  xor xor_10 (xor_9_out[1], xor_6_out, or_5_out);
  and and_10 (and_10_out, xor_6_out, or_5_out);
  xor xor_11 (xor_9_out[2], xor_7_out, or_6_out);
  and and_11 (and_11_out, xor_7_out, or_6_out);
  xor xor_12 (xor_9_out[3], xor_8_out, or_7_out);
  and and_12 (and_12_out, xor_8_out, or_7_out);
  or or_5 (or_5_out, and_9_out, and_5_out);
  or or_6 (or_6_out, and_10_out, and_6_out);
  or or_7 (or_7_out, and_11_out, and_7_out);
  or or_8 (or_8_out, and_12_out, and_8_out);
  xor xor_13 (out_8, or_8_out, in_4);
  xor xor_14 (xor_14_out, A[0], A[1]);
  and and_13 (and_13_out, A[0], A[1]);
  xor xor_15 (xor_15_out, A[1], B[1]);
  and and_14 (and_14_out, A[1], B[1]);
  xor xor_16 (xor_16_out, A[2], B[2]);
  and and_15 (and_15_out, A[2], B[2]);
  xor xor_17 (xor_17_out, A[3], B[3]);
  and and_16 (and_16_out, A[3], B[3]);
  xor xor_18 (xor_18_out[0], xor_14_out, undriven);
  and and_17 (and_17_out, undriven, xor_14_out);
  xor xor_19 (xor_18_out[1], xor_15_out, or_9_out);
  and and_18 (and_18_out, or_9_out, xor_15_out);
  xor xor_20 (xor_18_out[2], xor_16_out, or_10_out);
  and and_19 (and_19_out, or_10_out, xor_16_out);
  xor xor_21 (xor_18_out[3], xor_17_out, or_11_out);
  and and_20 (and_20_out, or_11_out, xor_17_out);
  or or_9 (or_9_out, and_17_out, and_13_out);
  or or_10 (or_10_out, and_18_out, and_14_out);
  or or_11 (or_11_out, and_19_out, and_15_out);
  or or_12 (out_6, and_20_out, and_16_out);
  Multiplexer #(.select(2), .width(4)) multiplexer_1 (
    .in0(xor_18_out), .in1(xor_9_out), .in2(and_4_out), .in3(or_4_out), .out(out_7), .en(undriven_2));  // open: sel

  assign B[0] = A[1];
endmodule
