// Logisim project ALUandRegister.circ as structural Verilog: 1 circuit, main circuit main
module main (
  input  Clock,
  input  Data_Input_D3,
  input  Control__Enable,
  input  Data_Input_D2,
  input  Data_Input_D1,
  input  Data_Input_D0,
  input  [3:0] _4bit,
  input  [3:0] _4bit_2,
  input  Data_Input_D3_2,
  input  [1:0] Selector_Bit,
  input  Data_Input_D2_2,
  input  Data_Input_D1_2,
  input  Data_Input_D0_2,
  output [3:0] _4bit_Output
);

  wire d_ff_1_q, d_ff_2_q, d_ff_3_q, d_ff_4_q, d_ff_5_q, d_ff_6_q, d_ff_7_q, d_ff_8_q, multiplexer_1_out,
       multiplexer_2_out;
  wire [3:0] adder_1_out, AND_out, OR_out, subtractor_1_out;

  D_Flip_Flop d_ff_1 (.clk(Clock), .D(Data_Input_D3_2), .Q(d_ff_1_q), .en(Control__Enable));  // open: Qn, preset, reset
  D_Flip_Flop d_ff_2 (.clk(Clock), .D(Data_Input_D2_2), .Q(d_ff_2_q), .en(Control__Enable));  // open: Qn, preset, reset
  D_Flip_Flop d_ff_3 (.clk(Clock), .D(Data_Input_D1_2), .Q(d_ff_3_q), .en(Control__Enable));  // open: Qn, preset, reset
  D_Flip_Flop d_ff_4 (.clk(Clock), .D(Data_Input_D0_2), .Q(d_ff_4_q), .en(Control__Enable));  // open: Qn, preset, reset
  D_Flip_Flop d_ff_5 (.clk(Clock), .D(Data_Input_D3), .Q(d_ff_5_q), .en(Control__Enable));  // open: Qn, preset, reset
  D_Flip_Flop d_ff_6 (.clk(Clock), .D(Data_Input_D2), .Q(d_ff_6_q), .en(Control__Enable));  // open: Qn, preset, reset
  D_Flip_Flop d_ff_7 (.clk(Clock), .D(Data_Input_D1), .Q(d_ff_7_q), .en(Control__Enable));  // open: Qn, preset, reset
  D_Flip_Flop d_ff_8 (.clk(Clock), .D(Data_Input_D0), .Q(d_ff_8_q), .en(Control__Enable));  // open: Qn, preset, reset
  Multiplexer multiplexer_1 (.in0(d_ff_5_q), .in1(d_ff_6_q), .out(multiplexer_1_out), .sel(d_ff_7_q), .en(d_ff_8_q));
  Multiplexer multiplexer_2 (.in0(d_ff_1_q), .in1(d_ff_2_q), .out(multiplexer_2_out), .sel(d_ff_3_q), .en(d_ff_4_q));
  Adder #(.width(4)) adder_1 (.a(_4bit), .b(_4bit_2), .out(adder_1_out));  // open: cin, cout
  Subtractor #(.width(4)) subtractor_1 (.a(_4bit), .b(_4bit_2), .out(subtractor_1_out));  // open: bin, bout
  assign AND_out = _4bit & _4bit_2;  // AND_Gate AND, 4 bits wide
  assign OR_out = _4bit | _4bit_2;  // OR_Gate OR, 4 bits wide
  Multiplexer #(.select(2), .width(4), .enable("false")) multiplexer_3 (
    .in0(adder_1_out), .in1(subtractor_1_out), .in2(AND_out), .in3(OR_out), .out(_4bit_Output),
    .sel(Selector_Bit));

  // Notes on the sheet:
  //   4 Bit Register
  //   4 Bit Register
  //   D Flip Flop
  //   D Flip Flop
  //   D Flip Flop
  //   D Flip Flop
  //   D Flip Flop
  //   D Flip Flop
  //   D Flip Flop
  //   D Flip Flop
  //   Q1
  //   Q2
  //   Q3
  //   Q0
  //   Q1
  //   Q2
  //   Q3
  //   Q0
  //   Input A
  //   Input B
  //   ALU Circuit with Add, Subtract, AND, OR functions
  //   4bit Adder
  //   4bit Subtractor
endmodule
