// Logisim project ALUwithAddSubANDOR.circ as structural Verilog: 1 circuit, main circuit main
module main (
  input  [3:0] _4bit,
  input  [3:0] Input_B,
  input  [1:0] Selector_Bit,
  output [3:0] _4bit_Output
);

  wire [3:0] adder_1_out, AND_out, OR_out, subtractor_1_out;

  Adder #(.width(4)) adder_1 (.a(_4bit), .b(Input_B), .out(adder_1_out));  // open: cin, cout
  Subtractor #(.width(4)) subtractor_1 (.a(_4bit), .b(Input_B), .out(subtractor_1_out));  // open: bin, bout
  assign AND_out = _4bit & Input_B;  // AND_Gate AND, 4 bits wide
  assign OR_out = _4bit | Input_B;  // OR_Gate OR, 4 bits wide
  Multiplexer #(.select(2), .width(4), .enable("false")) multiplexer_1 (
    .in0(adder_1_out), .in1(subtractor_1_out), .in2(AND_out), .in3(OR_out), .out(_4bit_Output),
    .sel(Selector_Bit));

  // Notes on the sheet:
  //   Input A
  //   4bit
  //   4bit Adder
  //   4bit Subtractor
  //   ALU Circuit with Add, Subtract, AND, OR functions
endmodule
