// Logisim project AdderTwoFourBitNums.circ as structural Verilog: 1 circuit, main circuit main
module main (
  input  Carry_in,
  input  [3:0] A,
  input  [3:0] B,
  output [3:0] out_4,
  output Carry_out
);

  wire NAND_2_out, NAND_3_out, NAND_4_out, NAND_5_out, NAND_6_out, NAND_7_out, NAND_8_out, NAND_9_out,
       NAND_10_out, NAND_11_out, NAND_12_out, NAND_13_out, NAND_14_out, NAND_15_out, NAND_16_out,
       NAND_17_out, NAND_18_out, NAND_19_out, NAND_20_out, NAND_21_out, NAND_23_out, NAND_24_out,
       NAND_25_out, NAND_26_out, NAND_27_out, NAND_28_out, NAND_29_out, NAND_30_out, NAND_31_out,
       NAND_32_out, NAND_out;
  wire [3:0] NAND_34_out;

  nand NAND (NAND_out, A[3], B[3]);
  nand NAND_2 (NAND_2_out, A[0], B[0]);
  nand NAND_3 (NAND_3_out, A[1], B[1]);
  nand NAND_4 (NAND_4_out, A[3], NAND_out);
  nand NAND_5 (NAND_5_out, NAND_out, B[3]);
  nand NAND_6 (NAND_6_out, A[0], NAND_2_out);
  nand NAND_7 (NAND_7_out, NAND_2_out, B[0]);
  nand NAND_8 (NAND_8_out, A[2], B[2]);
  nand NAND_9 (NAND_9_out, A[1], NAND_3_out);
  nand NAND_10 (NAND_10_out, B[1], B[1], NAND_3_out);
  nand NAND_11 (NAND_11_out, B[2], NAND_8_out);
  nand NAND_12 (NAND_12_out, NAND_4_out, NAND_5_out);
  nand NAND_13 (NAND_13_out, NAND_6_out, NAND_7_out);
  nand NAND_14 (NAND_14_out, NAND_9_out, NAND_10_out);
  nand NAND_15 (NAND_15_out, A[2], NAND_8_out);
  nand NAND_16 (NAND_16_out, NAND_15_out, NAND_11_out);
  nand NAND_17 (NAND_17_out, Carry_in, NAND_13_out);
  nand NAND_18 (NAND_18_out, NAND_32_out, NAND_12_out);
  nand NAND_19 (NAND_19_out, NAND_25_out, NAND_14_out);
  nand NAND_20 (NAND_20_out, NAND_32_out, NAND_18_out);
  nand NAND_21 (NAND_21_out, NAND_18_out, NAND_12_out);
  nand NAND_22 (Carry_out, NAND_18_out, NAND_out);
  nand NAND_23 (NAND_23_out, Carry_in, NAND_17_out);
  nand NAND_24 (NAND_24_out, NAND_17_out, NAND_13_out);
  nand NAND_25 (NAND_25_out, NAND_17_out, NAND_2_out);
  nand NAND_26 (NAND_26_out, NAND_29_out, NAND_16_out);
  nand NAND_27 (NAND_27_out, NAND_25_out, NAND_19_out);
  nand NAND_28 (NAND_28_out, NAND_19_out, NAND_14_out);
  nand NAND_29 (NAND_29_out, NAND_19_out, NAND_3_out);
  nand NAND_30 (NAND_30_out, NAND_29_out, NAND_26_out);
  nand NAND_31 (NAND_31_out, NAND_26_out, NAND_16_out);
  nand NAND_32 (NAND_32_out, NAND_26_out, NAND_8_out);
  nand NAND_33 (NAND_34_out[3], NAND_20_out, NAND_21_out);
  nand NAND_34 (NAND_34_out[0], NAND_23_out, NAND_24_out);
  nand NAND_35 (NAND_34_out[1], NAND_27_out, NAND_28_out);
  nand NAND_36 (NAND_34_out[2], NAND_30_out, NAND_31_out);

  // Notes on the sheet:
  //   Sum
  //   Sum
  //   Sum
  //   Sum
endmodule
