// Logisim project AlarmSystem.circ as structural Verilog: 1 circuit, main circuit main
module main (
  input  Armed,
  input  Doors,
  input  Glass,
  input  Motion,
  output out_5
);

  wire OR_out;

  or OR (OR_out, Doors, Glass, Motion);
  and AND (out_5, Armed, Armed, OR_out);

  // Notes on the sheet:
  //   Alarm system circuit using 2 logic gates
endmodule
