// Logisim project SecondAssignment.circ as structural Verilog: 1 circuit, main circuit main
module main (
  input  A,
  input  B,
  input  C,
  output out_4
);

  wire AND_2_out, AND_out, not_1_out, not_2_out;

  not not_1 (not_1_out, A);
  not not_2 (not_2_out, B);
  and AND (AND_out, not_1_out, B, C);
  and AND_2 (AND_2_out, C, C, not_2_out, A);
  or OR (out_4, AND_out, AND_2_out);

  // Notes on the sheet:
  //   NOT GATE
  //   NOT GATE
endmodule
