// Logisim project SubtractorAndAdder.circ as structural Verilog: 1 circuit, main circuit main
module main (
  input  Carry_in,
  input  [3:0] A,
  input  in_3,
  input  [3:0] B,
  input  [3:0] in_5,
  output [3:0] out_6,
  output Carry_out
);

  wire AND_2_out, AND_3_out, AND_4_out, AND_5_out, AND_6_out, AND_7_out, AND_8_out, AND_out, OR_2_out,
       OR_3_out, OR_out, undriven, XOR_2_out, XOR_3_out, XOR_4_out, XOR_out;
  wire [3:0] adder_1_out, not_1_out;

  assign not_1_out = ~B;  // NOT_Gate not_1, 4 bits wide
  Adder #(.width(4)) adder_1 (.a(not_1_out), .b(in_5), .out(adder_1_out), .cin(undriven));  // open: cout
  xor XOR (XOR_out, A[0], adder_1_out[0]);
  and AND (AND_out, adder_1_out[0], A[0]);
  xor XOR_2 (XOR_2_out, A[1], adder_1_out[1]);
  and AND_2 (AND_2_out, adder_1_out[1], A[1]);
  xor XOR_3 (XOR_3_out, A[2], adder_1_out[2]);
  and AND_3 (AND_3_out, adder_1_out[2], A[2]);
  xor XOR_4 (XOR_4_out, A[3], adder_1_out[3]);
  and AND_4 (AND_4_out, adder_1_out[3], A[3]);
  xor XOR_5 (out_6[0], XOR_out, Carry_in);
  and AND_5 (AND_5_out, Carry_in, XOR_out);
  xor XOR_6 (out_6[1], XOR_2_out, OR_out);
  and AND_6 (AND_6_out, OR_out, XOR_2_out);
  xor XOR_7 (out_6[2], XOR_3_out, OR_2_out);
  and AND_7 (AND_7_out, OR_2_out, XOR_3_out);
  xor XOR_8 (out_6[3], XOR_4_out, OR_3_out);
  and AND_8 (AND_8_out, OR_3_out, XOR_4_out);
  or OR (OR_out, AND_5_out, AND_out);
  or OR_2 (OR_2_out, AND_6_out, AND_2_out);
  or OR_3 (OR_3_out, AND_7_out, AND_3_out);
  or OR_4 (Carry_out, AND_8_out, AND_4_out);

  // Notes on the sheet:
  //   NOT
endmodule
