// Logisim project ThirdAssignment.circ as structural Verilog: 1 circuit, main circuit main
module main (
  input  A,
  input  B,
  input  C,
  output out_4
);

  wire AND_2_out, AND_out, NOR_2_out, NOR_out, OR_2_out, OR_out;

  nor NOR (NOR_out, A, B);
  and AND (AND_out, A, B);
  or OR (OR_out, NOR_out, AND_out);
  and AND_2 (AND_2_out, OR_out, C);
  nor NOR_2 (NOR_2_out, OR_out, C);
  or OR_2 (OR_2_out, NOR_2_out, AND_2_out);
  not not_1 (out_4, OR_2_out);

  // Notes on the sheet:
  //   NOT Gate
endmodule
