// Logisim project XORGate.circ as structural Verilog: 1 circuit, main circuit main
module main (
  input  in_1,
  input  in_2,
  output out_3
);

  wire NAND_2_out, NAND_3_out, NAND_4_out, NAND_out;

  nand NAND (NAND_out, in_1, in_2);
  nand NAND_2 (NAND_2_out, in_1, NAND_out);
  nand NAND_3 (NAND_3_out, NAND_out, in_2);
  nand NAND_4 (NAND_4_out, NAND_2_out, NAND_3_out);
  not not_1 (out_3, NAND_4_out);

  // Notes on the sheet:
  //   Exclusive-OR
endmodule
